# Fritzing sketch Scanner3D (saved by Fritzing 0.9.1b)
breadboards: 1

parts:
  Part1 = Arduino Uno (Rev3)
  LED1 = LED - 5mm [color="Green (560nm)" package="5 mm [THT]"]
  J1 = Basic Servo
  J2 = Basic Servo
  LED2 = LED - 5mm [color="Red (633nm)" package="5 mm [THT]"]
  R1 = Resistor [tolerance=±5% resistance=220 package=THT]  # not connected
  R2 = Resistor [tolerance=±5% resistance=220 package=THT]  # not connected
  S1 = Pushbutton [package="[THT]"]
  Infared_Distance_Sensor = Infrared Proximity Sensor

nets:
  N1: Part1.A0, Infared_Distance_Sensor.Vout
  N2: Part1.D8, LED1.anode
  N3: Part1.D9_PWM, J2.pulse
  N4: Part1.D2, S1.Pin_3, S1.Pin_4
  N5: Part1.D6_PWM, J1.pulse
  N6: Part1.D7, LED2.anode
  GND: J1.gnd, J2.gnd, S1.Pin_1, S1.Pin_2, Infared_Distance_Sensor.GND
  5V: J1.vcc, J2.vcc, Infared_Distance_Sensor.Vcc
